# Fritzing sketch Machine control Rev M (saved by Fritzing 1.0.1rc)
circuit board: 10.1cm x 8.25cm
breadboards: 1

parts:
  D4 = Rectifier Diode [part_number=1N4001 package="300 mil [THT]"]
  C11 = Electrolytic Capacitor [capacitance=47µF voltage=50V package="100 mil [THT, electrolytic]"]
  C10 = Electrolytic Capacitor [capacitance=0.47mF voltage=35V package="100 mil [THT, electrolytic]"]
  R28 = Resistor [tolerance=±5% resistance=1.2k power=0.25 package=THT]
  R29 = Resistor [tolerance=±5% resistance=1.2k power=0.25 package=THT]
  R15 = Resistor [tolerance=±5% resistance=680 power=0.25 package=THT]
  C2 = Ceramic Capacitor [capacitance=100nF voltage=35V package="100 mil [THT, multilayer]"]
  C12 = Electrolytic Capacitor [capacitance=0.1mF voltage=50V package="100 mil [THT, electrolytic]"]
  Steer = LED - 5mm [color="Red (633nm)" current=0.030 package="5 mm [THT]"]
  R22 = Resistor [tolerance=±5% resistance=470 power=0.25 package=THT]
  R21 = Resistor [tolerance=±5% resistance=470 power=0.25 package=THT]
  Power = LED - 5mm [color="Green (555nm)" current=0.030 package="5 mm [THT]"]
  R20 = Resistor [tolerance=±5% resistance=470 power=0.25 package=THT]
  Wifi = LED - 5mm [color="Yellow (595nm)" current=0.030 package="5 mm [THT]"]
  ESP32 = ESP32-38PinWide [part_number=ESP32-38PinWide]
  Work = LED - 5mm [color="Blue (525nm)" current=0.030 package="5 mm [THT]"]
  R10 = Resistor [tolerance=±5% resistance=4.7k power=0.25 package=THT]
  Str_Sw = LED - 5mm [color="Yellow (595nm)" current=0.030 package="5 mm [THT]"]
  Wrk_Sw = LED - 5mm [color="Yellow (595nm)" current=0.030 package="5 mm [THT]"]
  MCP2562 = IC, DIP package, 8 pins [chip_label=IC]
  C5 = Ceramic Capacitor [capacitance=100nF voltage=35V package="100 mil [THT, multilayer]"]
  D7 = Rectifier Diode 600mil [part_number=1N5400 package="600 mil [THT]"]
  Disengage = LED - 5mm [color="Yellow (595nm)" current=0.030 package="5 mm [THT]"]
  H0 = DTM13-12PA-12PB-R008 [package=THT]
  R63 = Resistor [tolerance=±5% resistance=1k power=0.25 package=THT]
  R64 = Resistor [tolerance=±5% resistance=1k power=0.25 package=THT]
  R65 = Resistor [tolerance=±5% resistance=1k power=0.25 package=THT]
  R16 = Resistor [tolerance=±5% resistance=680 power=0.25 package=THT]
  TC4427 = TC4427 [part_number=TC4427 package="DIP (Dual Inline) [THT]"]
  78E05 = Voltage Regulator - 5V [package="TO220 [THT]"]
  C1 = Ceramic Capacitor [capacitance=100nF voltage=35V package="100 mil [THT, multilayer]"]
  R56 = Resistor [tolerance=±5% power=0.25 resistance=10k package=THT]
  R1 = Resistor [tolerance=±0.1% power=0.25 resistance=2.2k package=THT]
  R3 = Resistor [tolerance=±0.1% power=0.25 resistance=10k package=THT]
  D13 = BAV99 [package=sot23]
  D11 = BAV99 [package=sot23]
  F3 = Fuse PCB mount [package=THT]
  R6 = Resistor [tolerance=±0.1% resistance=3.3k power=0.25 package=THT]
  R5 = Resistor [tolerance=±0.1% resistance=3.3k power=0.25 package=THT]
  D19 = BAV99 [package=sot23]
  D20 = BAV99 [package=sot23]
  ADS1115 = Adafruit ADS1115 16-Bit ADC [part_number=1085]
  D10 = BAV99 [package=sot23]
  R45 = Resistor [tolerance=±5% power=0.25 resistance=10k package=THT]
  R25 = Resistor [tolerance=±0.1% power=0.25 resistance=5.6k package=THT]
  R26 = Resistor [tolerance=±0.1% power=0.25 resistance=5.6k package=THT]
  J0 = Resistor [tolerance=±5% power=0.25 resistance=0 package=THT]
  R67 = Resistor [tolerance=±5% resistance=1k power=0.25 package=THT]
  R50 = Resistor [tolerance=±5% power=0.25 resistance=270 package=THT]
  R51 = Resistor [tolerance=±5% power=0.25 resistance=270 package=THT]
  D17 = BAV99 [package=sot23]
  D18 = BAV99 [package=sot23]
  D21 = BAV99 [package=sot23]
  R42 = Resistor [tolerance=±5% power=0.25 resistance=10k package=THT]
  R41 = Resistor [tolerance=±5% power=0.25 resistance=1k package=THT]
  R40 = Resistor [tolerance=±5% power=0.25 resistance=1k package=THT]
  R44 = Resistor [tolerance=±5% power=0.25 resistance=10k package=THT]
  R43 = Resistor [tolerance=±5% power=0.25 resistance=10k package=THT]
  R53 = Resistor [tolerance=±5% power=0.25 resistance=680 package=THT]
  R46 = Resistor [tolerance=±5% power=0.25 resistance=10k package=THT]
  Flow = LED - 5mm [color="Yellow (595nm)" current=0.030 package="5 mm [THT]"]
  D14 = BAV99 [package=sot23]
  F2 = Fuse PCB mount [package=THT]
  uni/sep = IC, SIP package, 3 pins [chip_label=IC]
  R66 = Resistor [tolerance=±5% power=0.25 resistance=1k package=THT]
  R58 = Resistor [tolerance=±5% resistance=1k power=0.25 package=THT]
  R59 = Resistor [tolerance=±5% resistance=1k power=0.25 package=THT]
  R60 = Resistor [tolerance=±5% resistance=1k power=0.25 package=THT]
  U4 = U [package=dpak-5]
  R61 = Resistor [tolerance=±5% resistance=1k power=0.25 package=THT]
  R23 = Resistor [tolerance=±5% power=0.25 resistance=470 package=THT]
  3906 = PNP-Transistor [part_number=2N3906 package="TO92 [THT]"]
  R47 = Resistor [tolerance=±5% power=0.25 resistance=10k package=THT]
  D24 = Rectifier Diode [part_number=1N4001 package="300 mil [THT]"]
  D25 = Rectifier Diode [part_number=1N4001 package="300 mil [THT]"]
  R68 = Resistor [tolerance=±5% resistance=1k power=0.25 package=THT]
  R69 = Resistor [tolerance=±5% resistance=1k power=0.25 package=THT]
  Q1 = N-channel mosfet [part_number=VN2410L-G package="TO92 [THT]"]
  Q2 = N-channel mosfet [part_number=VN2410L-G package="TO92 [THT]"]
  F5305 = Basic FET P-Channel [package="DPak [SMD]"]
  F5305_2 = Basic FET P-Channel [package="DPak [SMD]"]
  R62 = Resistor [tolerance=±5% resistance=1k power=0.25 package=THT]
  R57 = Resistor [tolerance=±5% power=0.25 resistance=10k package=THT]
  U5 = INVERTER [mpn=MIC2005A-1YM5 package=sot23-5]
  R19 = Resistor [tolerance=±5% power=0.25 resistance=470 package=THT]
  C13 = Ceramic Capacitor [capacitance=100nF voltage=35V package="100 mil [THT, multilayer]"]
  C3 = Ceramic Capacitor [capacitance=100nF voltage=35V package="100 mil [THT, multilayer]"]
  C4 = Ceramic Capacitor [capacitance=100nF voltage=35V package="100 mil [THT, multilayer]"]
  D21_2 = BAV99 [package=sot23]
  D22 = BAV99 [package=sot23]
  U6 = U [package=THT]
  R70 = Resistor [tolerance=±5% resistance=1k power=0.25 package=THT]
  R71 = Resistor [tolerance=±5% resistance=1k power=0.25 package=THT]
  Tx = LED - 5mm [color="Yellow (595nm)" current=0.030 package="5 mm [THT]"]
  Rx = LED - 5mm [color="Yellow (595nm)" current=0.030 package="5 mm [THT]"]
  J1 = female pin header, 2 pins [form="♀ (female)"]
  R75 = Resistor [tolerance=±5% power=0.25 resistance=120 package=THT]

nets:
  N1: D4.cathode, C11.+, 78E05.input_voltage
  N2: D4.anode, H0.pin_2
  GND: C11.-, C10.-, C12.-, Steer.cathode, Power.cathode, Wifi.cathode, ESP32.GND, Work.cathode, MCP2562.pin2, C5.0, H0.pin_3, H0.pin_4, H0.pin_13, H0.pin_23, H0.pin_24, R63.Pin_0, R64.Pin_0, R65.Pin_0, TC4427.GND, 78E05.GND, R1.Pin_1, D13.A1, D11.A1, ADS1115.GND, D10.A1, R25.Pin_0, R26.Pin_0, R50.Pin_0, R51.Pin_0, D17.A1, D18.A1, D21.A1, R42.Pin_0, Flow.cathode, D14.A1, R66.Pin_1, R58.Pin_0, R59.Pin_0, U4.Gnd, R23.Pin_0, D24.anode, D25.anode, Q1.S, Q2.S, U5.A, U6.Gnd
  VIN: C10.+, R20.Pin_1, ESP32.VIN, MCP2562.pin3, C5.1, 78E05.output_voltage, R56.Pin_1, F3.pin2, U5.NC, U6.5V
  N3: R28.Pin_0, ESP32.GPIO22, ADS1115.SCL
  N4: R28.Pin_1, R29.Pin_1, ESP32.3.3, MCP2562.pin5, D13.C2, D11.C2, D10.C2, J0.Pin_1, D17.C2, D18.C2, D14.C2, C13.0, Tx.anode, Rx.anode
  N5: R29.Pin_0, ESP32.GPIO21, ADS1115.SDA
  N6: R15.Pin_0, Str_Sw.anode
  N7: R15.Pin_1, uni/sep.pin2
  N8: C2.0, C1.0, D19.A1, D20.A1, ADS1115.AGND, C3.0, C4.0, D21_2.A1, D22.A1
  N9: C2.1, D20.COM, ADS1115.AIN1, R44.Pin_0
  N10: C12.+, D7.cathode, TC4427.VDD, R3.Pin_0, uni/sep.pin1, U4.Vs, R68.Pin_1, R69.Pin_1, F5305.source, F5305_2.source
  N11: Steer.anode, R22.Pin_0
  N12: R22.Pin_1, ESP32.GPIO12
  N13: R21.Pin_0, Wifi.anode
  N14: R21.Pin_1, ESP32.GPIO13
  N15: Power.anode, R20.Pin_0
  N16: ESP32.GPIO36, D10.COM, R45.Pin_0
  N17: ESP32.GPIO39, D11.COM, R46.Pin_0
  N18: ESP32.GPIO34, D13.COM, R57.Pin_1, C13.1
  N19: ESP32.GPIO35, D14.COM, R58.Pin_1
  N20: ESP32.GPIO32, R59.Pin_1, U5.GND
  N21: ESP32.GPIO33, R60.Pin_1
  N22: ESP32.GPIO25, R65.Pin_1, R62.Pin_1
  N23: ESP32.GPIO26, R64.Pin_1, R61.Pin_1
  N24: ESP32.GPIO27, R63.Pin_1, TC4427.IN_B
  N25: ESP32.GPIO14, R10.Pin_1
  N26: ESP32.GPIO15, D18.COM, R40.Pin_1
  N27: ESP32.GPIO2, D17.COM, R41.Pin_1
  N28: ESP32.GPIO0, U6.Cs
  N29: ESP32.GPIO16, U6.MISO
  N30: ESP32.GPIO17, U6.MOSI
  N31: ESP32.GPIO5, U6.Sck
  N32: ESP32.GPIO18, MCP2562.pin4, R70.Pin_1
  N33: ESP32.GPIO19, MCP2562.pin1, R71.Pin_1
  N34: ESP32.GPIO23, Disengage.anode, D21.COM, R42.Pin_1, 3906.C
  N35: Work.anode, R10.Pin_0
  N36: Str_Sw.cathode, R50.Pin_1, R40.Pin_0
  N37: Wrk_Sw.cathode, R51.Pin_1, R41.Pin_0
  N38: Wrk_Sw.anode, R16.Pin_0
  N39: MCP2562.pin6, H0.pin_14, R75.Pin_1
  N40: MCP2562.pin7, H0.pin_15, J1.pin1
  N41: MCP2562.pin8, R66.Pin_0
  N42: D7.anode, H0.pin_1
  N43: Disengage.cathode, R23.Pin_1
  N44: H0.pin_5, R16.Pin_1
  N45: H0.pin_6, F2.pin1
  N46: H0.pin_7, R67.Pin_1
  N47: H0.pin_8, D25.cathode, F5305_2.drain
  N48: H0.pin_9, D24.cathode, F5305.drain
  N49: H0.pin_10, U4.Out
  N50: H0.pin_11, R53.Pin_1
  N51: H0.pin_12, uni/sep.pin3
  N52: H0.pin_16, U6.CanH
  N53: H0.pin_17, U6.CanL
  N54: H0.pin_18, H0.pin_19, F3.pin1, R45.Pin_1
  N55: H0.pin_20, R5.Pin_1
  N56: H0.pin_21, R6.Pin_1
  N57: H0.pin_22, R56.Pin_0, R47.Pin_0, R19.Pin_1, U6.Disengage
  N58: TC4427.OUT_B, R67.Pin_0
  N59: TC4427.OUT_A, F2.pin2
  N60: C1.1, D19.COM, ADS1115.AIN0, R43.Pin_0
  N61: R1.Pin_0, R3.Pin_1, R57.Pin_0
  N62: R6.Pin_0, R25.Pin_1, R43.Pin_1
  N63: R5.Pin_0, R26.Pin_1, R44.Pin_1
  N64: D19.C2, D20.C2, ADS1115.AVDD, D21_2.C2, D22.C2
  N65: ADS1115.AIN3, C4.1, D22.COM, U6.A1
  N66: ADS1115.AIN2, C3.1, D21_2.COM, U6.A0
  VCC: ADS1115.VCC, J0.Pin_0, D21.C2, 3906.E, U6.3.3V
  N67: R53.Pin_0, R46.Pin_1, Flow.anode
  N68: R60.Pin_0, U4.In
  N69: R61.Pin_0, Q2.G
  N70: 3906.B, R47.Pin_1
  N71: R68.Pin_0, Q2.D, F5305_2.Gate
  N72: R69.Pin_0, Q1.D, F5305.Gate
  N73: Q1.G, R62.Pin_0
  N74: U5.VCC, R19.Pin_0
  N75: R70.Pin_0, Rx.cathode
  N76: R71.Pin_0, Tx.cathode
  N77: J1.pin2, R75.Pin_0

notes:
  Rev M
  Copyright Reuben Rissler 2025
  License GPLv3 - PCB design
  A- A0 A1 A2 A3 A+
  SCL
  SDA
  GND
  VIN
  ADDR
  ALRT
  Gnd
  5V A1 A0 Dis Gnd
  12s 12L Grnd Wrk Alm
  Str Flw Lck Out Out Dan
  5V 2chan CnBs1 Gnd
  H
  L
  Sck
  Mosi
  Miso
  Cs

custom parts:
  ESP32-38PinWide: Generic 38-Pin ESP32 with wide format (only access to one side of pins on a breadboard) based on Stephen Lilley's HiLetgo ESP-WROOM-32 ESP32 ESP-32S Development Board.
  Rectifier Diode 600mil: A standard 3amp rectifier diode
  DTM13-12PA-12PB-R008: DTM13-12PA-12PB-R008 connector.
  TC4427: A 1.5 amp high side mosfet driver useful for driving positive loads from a microcontroller
  Voltage Regulator - 5V: 5V DC Voltage Regulator
  Fuse PCB mount: A PCB mount fuse with 200 mil spacing.
  Adafruit ADS1115 16-Bit ADC: For microcontrollers without an analog-to-digital converter or when you want a higher-precision ADC, the ADS1115 provides 16-bit precision at 860 samples/second over I2C. The chip can be configured as 4 single-ended input channels, or two differential channels. As a nice bonus, it even includes a programmable gain amplifier, up to x16, to help boost up smaller single/differential signals to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
  U: BTF50060 - a P-Channel smart switch in a DPAK-5 package
  N-channel mosfet: A TO-92 N-channel mosfet
  U: CanBus adapter using MCP2515 and MCP2562, alternatively have dual analog voltage inputs
