# Fritzing sketch Row sense Rev B (saved by Fritzing 1.0.1rc)
circuit board: 3.5cm x 2cm
breadboards: 1

parts:
  U2 = mystery part, 5 pins [chip_label=?]
  U1 = mystery part, 7 pins [chip_label=?]
  R5 = Resistor [tolerance=±0.1% power=0.25 resistance=10k package=THT]
  R3 = Resistor [tolerance=±0.1% power=0.25 resistance=5.6k package=THT]
  R6 = Resistor [tolerance=±0.1% power=0.25 resistance=10k package=THT]
  R4 = Resistor [tolerance=±0.1% power=0.25 resistance=5.6k package=THT]
  R2 = Resistor [tolerance=±0.1% resistance=3.3k power=0.25 package=THT]
  R1 = Resistor [tolerance=±0.1% resistance=3.3k power=0.25 package=THT]
  R7 = Resistor [tolerance=±0.1% power=0.25 resistance=1k package=THT]
  R8 = Resistor [tolerance=±0.1% power=0.25 resistance=1k package=THT]

nets:
  N1: U2.pin1, R3.Pin_0, R4.Pin_0, R7.Pin_1, R8.Pin_1
  N2: U2.pin4, R1.Pin_1, R7.Pin_0
  N3: U2.pin5, R2.Pin_1, R8.Pin_0
  N4: U1.pin6, R5.Pin_0
  N5: U1.pin7, R6.Pin_0
  N6: R5.Pin_1, R4.Pin_1, R1.Pin_0
  N7: R3.Pin_1, R6.Pin_1, R2.Pin_0

notes:
  Row sense
  Gnd
  Ch3
  A2
  A3
  Ch2
  Rev B
