# Fritzing sketch Power control compact Rev D (saved by Fritzing 1.0.1rc)
circuit board: 6.2cm x 8.25cm
breadboards: 1

parts:
  D1 = Rectifier Diode [part_number=1N4001 package="300 mil [THT]"]
  LED1 = LED - 5mm [color="Green (560nm)" current=0.030 package="5 mm [THT]"]
  TINY45 = attiny85 [package=dip]
  D4 = Rectifier Diode [part_number=1N4001 package="300 mil [THT]"]
  OMRON = OMRON PCB Power Relay – G5LE [part_number="G5LE-1\n" package=THT]
  C1 = Electrolytic Capacitor [capacitance=0.1mF voltage=6.3V package="100 mil [THT, electrolytic]"]
  C2 = Electrolytic Capacitor [capacitance=1µF voltage=35V package="100 mil [THT, electrolytic]"]
  R1 = Resistor [tolerance=±5% power=0.25 resistance=330 package=THT]
  R3 = Resistor [tolerance=±0.1% power=0.25 resistance=4.7k package=THT]
  R8 = Resistor [tolerance=±0.1% power=0.25 resistance=10k package=THT]
  TC4427 = TC4427 [part_number=TC4427 package="DIP (Dual Inline) [THT]"]
  D2 = Rectifier Diode [part_number=1N4001 package="300 mil [THT]"]
  R5 = Resistor [tolerance=±0.1% power=0.25W resistance=10k package=THT]
  R6 = Resistor [tolerance=±1% power=0.25W resistance=105k package=THT]
  C7 = Ceramic Capacitor [capacitance=100nF voltage=35V package="100 mil [THT, multilayer]"]
  D6 = Rectifier Diode 600mil [part_number=1N5400 package="600 mil [THT]"]
  C4 = Electrolytic Capacitor [capacitance=0.47mF voltage=35V package="200 mil [THT, electrolytic]"]
  Max1771 = mystery part, 8 pins [chip_label=? mpn=MAX1771]
  C9 = Ceramic Capacitor [capacitance=100nF voltage=35V package="100 mil [THT, multilayer]"]
  2905 = Basic FET N-Channel [package="DPak [SMD]"]
  C3 = Electrolytic Capacitor [capacitance=0.47mF voltage=35V package="200 mil [THT, electrolytic]"]
  R15 = Resistor [tolerance=±5% resistance=40m power=0.25W package="2512 [SMD]"]
  C8 = Ceramic Capacitor [capacitance=100nF voltage=35V package="100 mil [THT, multilayer]"]
  D3 = Rectifier Diode [part_number=1N4001 package="300 mil [THT]"]
  R10 = Resistor [tolerance=±5% power=0.25 resistance=10k package=THT]
  7_5A_Max = Fuseholder [part_number=3568]
  F1 = female pin header, 2 pins [form="♀ (female)"]
  3A_Max = Fuseholder [part_number=3568]
  R11 = Resistor [tolerance=±5% power=0.25 resistance=10k package=THT]
  F2 = female pin header, 2 pins [form="♀ (female)"]
  C10 = Ceramic Capacitor [capacitance=100nF voltage=35V package="100 mil [THT, multilayer]"]
  L1 = Inductor [mpn=2205-H-RC package="[THT]"]
  78E05 = Voltage Regulator - 5V [package="TO220 [THT]"]
  -5V+ = screw terminal, 2 pins
  F3 = female pin header, 2 pins [form="♀ (female)"]
  J1 = DTM13-12PA-R008 [package=THT]

nets:
  N1: D1.cathode, C2.+, D2.cathode, 78E05.input_voltage, J1.pin_5
  N2: D1.anode, R8.Pin_0, F2.pin1
  GND: LED1.cathode, TINY45.Pin_4, D4.anode, OMRON.COIL1, C1.-, C2.-, R3.Pin_1, TC4427.GND, R5.Pin_1, C4.-, Max1771.pin4, Max1771.pin6, Max1771.pin7, C9.1, C3.-, R15.Pin_0, C8.0, R10.Pin_1, R11.Pin_1, 78E05.GND, -5V+.pin1, J1.pin_8, J1.pin_9, J1.pin_10, J1.pin_11, J1.pin_12
  N3: LED1.anode, R1.Pin_1
  N4: TINY45.Pin_1, TINY45.Pin_8, C1.+, C10.1, 78E05.output_voltage, F3.pin1
  N5: TINY45.Pin_2, R3.Pin_0, R8.Pin_1, C10.0
  N6: TINY45.Pin_3, TC4427.IN_B, R10.Pin_0
  N7: TINY45.Pin_6, R1.Pin_0
  N8: TINY45.Pin_7, TC4427.IN_A, R11.Pin_0
  N9: D4.cathode, OMRON.COIL2, TC4427.OUT_A
  N10: OMRON.A, 7_5A_Max.Connector1, 7_5A_Max.Connector3, F1.pin2
  N11: OMRON.C, C4.+, Max1771.pin2, C8.1, L1.pin_1
  N12: TC4427.OUT_B, D2.anode
  N13: TC4427.VDD, D3.cathode
  N14: R5.Pin_0, R6.Pin_0, C7.1, Max1771.pin3
  N15: R6.Pin_1, C7.0, D6.cathode, C3.+, J1.pin_1
  N16: D6.anode, 2905.drain, L1.pin_0
  N17: Max1771.pin1, 2905.Gate
  N18: Max1771.pin5, C9.0
  N19: Max1771.pin8, 2905.source, R15.Pin_1
  N20: D3.anode, F1.pin1
  N21: 7_5A_Max.Connector2, 7_5A_Max.Connector4, J1.pin_2
  N22: 3A_Max.Connector1, 3A_Max.Connector3, J1.pin_6
  N23: 3A_Max.Connector2, 3A_Max.Connector4, F2.pin2, J1.pin_3, J1.pin_4, J1.pin_7
  N24: -5V+.pin2, F3.pin2

notes:
  License GPLv3 - PCB design
  Ign Rtr 12Vout Bat 19V
  Copyright Reuben Rissler 2025
  Rev D
  12V Gnd Gnd Gnd Gnd Gnd

custom parts:
  TC4427: A 1.5 amp high side mosfet driver useful for driving positive loads from a microcontroller
  Rectifier Diode 600mil: A standard 3amp rectifier diode
  Fuseholder: Device used to protect against excessive current.
  Inductor: Inductor ferrite core
  Voltage Regulator - 5V: 5V DC Voltage Regulator
  DTM13-12PA-R008: DTM13-12PA-R008 connector.
